# Fritzing sketch memories_player (saved by Fritzing 0.9.3b)
circuit board: 4.15387cm x 4.53103cm
circuit board: 6.77334cm x 3.99142cm
breadboards: 1

parts:
  ENCODER1 = Rotary Encoder with Knob
  MCU1 = Raspberry Pi Zero
  SW1 = SWITCH-MOMENTARY-2 [package=tactile_switch_smd-2]
  to_raspiaudio_pin40 = female pin header, 1 pin [form="♀ (female)"]
  to_raspiaudio_pin35 = female pin header, 1 pin [form="♀ (female)"]
  to_raspiaudio_pin12 = female pin header, 1 pin [form="♀ (female)"]
  to_raspiaudio_pin39 = female pin header, 1 pin [form="♀ (female)"]
  to_raspiaudio_pin1 = female pin header, 1 pin [form="♀ (female)"]
  LED1 = smd LED [color="Blue (505nm)" package="1206 [SMD]"]
  R1 = Resistor [tolerance=±5% resistance=330 package="1206 [SMD]"]

nets (from the schematic view):
  N1: ENCODER1.no_name_yet#1, MCU1.pin_29
  N2: ENCODER1.no_name_yet#2, MCU1.pin_31
  N3: ENCODER1.no_name_yet#3, MCU1.pin_39, SW1.1, to_raspiaudio_pin39.pin1, LED1.cathode
  N4: ENCODER1.no_name_yet#4, MCU1.pin_37
  N5: ENCODER1.no_name_yet#5, MCU1.pin_2, MCU1.pin_4, SW1.2
  N6: MCU1.pin_1, to_raspiaudio_pin1.pin1
  N7: MCU1.pin_12, to_raspiaudio_pin12.pin1
  N8: MCU1.pin_13, R1.Pin_1
  N9: MCU1.pin_35, to_raspiaudio_pin35.pin1
  N10: MCU1.pin_40, to_raspiaudio_pin40.pin1
  N11: LED1.anode, R1.Pin_0

notes:
  A=CLK
  B=DT
  COM=GND
  SPST1A=SW
  SPST1B=+

custom parts:
  Rotary Encoder with Knob: Rotary Encoder with 1/4" Shaft and Knob
